// Logisim project trab.circ as structural Verilog: 3 circuits, main circuit main
module main (
);

  wire button_1_out, CLK, CONTROL_UNIT_rdm, not_1_out, not_2_out, STR;
  wire [1:0] CONTROL_UNIT_regaddr, RAMADDR;
  wire [4:0] counter_1_q;
  wire [7:0] ram_1_data, RAMIN, RAMOUT, rom_1_data;

  Clock clock_1 (.out(CLK));
  not not_1 (not_1_out, STR);
  Counter #(.width(5), .max('h1f)) counter_1 (
    .Q(counter_1_q), .clk(CLK), .clr(button_1_out));  // open: load, D, count, carry
  Button button_1 (.out(button_1_out));
  RAM #(.addrWidth(2), .bus("asynch")) ram_1 (.addr(RAMADDR), .data(ram_1_data), .ld(not_1_out));  // open: sel, clr
  not not_2 (not_2_out, STR);
  assign RAMOUT = not_2_out ? ram_1_data : 8'bz;  // Controlled_Buffer controlled_buffer_1
  assign ram_1_data = STR ? RAMIN : 8'bz;  // Controlled_Buffer controlled_buffer_2
  ROM #(.addrWidth(5)) rom_1 (.addr(counter_1_q), .data(rom_1_data));  // open: sel
  assign RAMOUT = STR ? {8{1'b0}} : 8'bz;  // Controlled_Buffer controlled_buffer_3
  CONTROL_UNIT CONTROL_UNIT (
    .INSTR(rom_1_data), .RDM(CONTROL_UNIT_rdm), .REGADDR(CONTROL_UNIT_regaddr), .RAMADDR(RAMADDR), .STR(STR));
  ALU alu_1 (
    .RDM(CONTROL_UNIT_rdm), .STR(STR), .REGADRR(CONTROL_UNIT_regaddr), .RAMOUT(RAMOUT), .CLK(CLK),
    .REGOUT(RAMIN));

  // Notes on the sheet:
  //   RAM
  //   ROM
  //   contents of rom_1 (hex, n*v repeats v):
  //   d0 d5 da df e3 e6 e9 ec
endmodule

module CONTROL_UNIT (
  input  [7:0] INSTR,
  output RDM,
  output [1:0] REGADDR,
  output [1:0] RAMADDR,
  output STR
);

  wire and_1_out, and_2_out, and_3_out, and_4_out, not_1_out, not_2_out;

  and and_1 (and_1_out, INSTR[7], INSTR[6]);
  and and_2 (and_2_out, INSTR[7], INSTR[6]);
  not not_1 (not_1_out, INSTR[5]);
  and and_3 (and_3_out, and_2_out, INSTR[5]);
  and and_4 (and_4_out, and_1_out, not_1_out);
  and and_5 (RDM, and_4_out, INSTR[4]);
  and and_6 (STR, and_3_out, not_2_out);
  not not_2 (not_2_out, INSTR[4]);
  assign REGADDR = STR ? INSTR[3:2] : 2'bz;  // Controlled_Buffer controlled_buffer_1
  assign REGADDR = RDM ? INSTR[3:2] : 2'bz;  // Controlled_Buffer controlled_buffer_2
  assign RAMADDR = STR ? INSTR[1:0] : 2'bz;  // Controlled_Buffer controlled_buffer_3
  assign RAMADDR = RDM ? INSTR[1:0] : 2'bz;  // Controlled_Buffer controlled_buffer_4
endmodule

module ALU (
  input  RDM,
  input  STR,
  input  [1:0] REGADRR,
  input  [7:0] RAMOUT,
  input  CLK,
  output [7:0] REGOUT
);

  wire and_1_out, and_2_out, and_3_out, and_4_out, and_5_out, and_6_out, and_7_out, and_8_out, not_1_out,
       not_2_out, not_3_out, not_4_out;
  wire [1:0] controlled_buffer_1_out;
  wire [7:0] controlled_buffer_3_out, controlled_buffer_5_out, controlled_buffer_7_out,
       controlled_buffer_13_out, REG00OUT, REG01OUT, REG10OUT, REG11OUT, register_1_q, register_2_q,
       register_3_q, register_4_q;

  assign controlled_buffer_1_out = RDM ? REGADRR : 2'bz;  // Controlled_Buffer controlled_buffer_1
  assign controlled_buffer_1_out = STR ? REGADRR : 2'bz;  // Controlled_Buffer controlled_buffer_2
  and and_1 (and_1_out, and_2_out, RDM);
  assign controlled_buffer_3_out = and_1_out ? RAMOUT : 8'bz;  // Controlled_Buffer controlled_buffer_3
  Register register_1 (.D(controlled_buffer_3_out), .Q(register_1_q), .clk(CLK));  // open: en, clr
  assign REG00OUT = and_2_out ? register_1_q : 8'bz;  // Controlled_Buffer controlled_buffer_4
  not not_1 (not_1_out, controlled_buffer_1_out[1]);
  not not_2 (not_2_out, controlled_buffer_1_out[0]);
  and and_2 (and_2_out, not_1_out, not_2_out);
  and and_3 (and_3_out, and_4_out, RDM);
  assign controlled_buffer_5_out = and_3_out ? RAMOUT : 8'bz;  // Controlled_Buffer controlled_buffer_5
  Register register_2 (.D(controlled_buffer_5_out), .Q(register_2_q), .clk(CLK));  // open: en, clr
  and and_4 (and_4_out, controlled_buffer_1_out[0], not_3_out);
  not not_3 (not_3_out, controlled_buffer_1_out[1]);
  assign REG01OUT = and_4_out ? register_2_q : 8'bz;  // Controlled_Buffer controlled_buffer_6
  and and_5 (and_5_out, and_6_out, RDM);
  assign controlled_buffer_7_out = and_5_out ? RAMOUT : 8'bz;  // Controlled_Buffer controlled_buffer_7
  not not_4 (not_4_out, controlled_buffer_1_out[0]);
  and and_6 (and_6_out, not_4_out, controlled_buffer_1_out[1]);
  assign REG10OUT = and_6_out ? register_3_q : 8'bz;  // Controlled_Buffer controlled_buffer_8
  Register register_3 (.D(controlled_buffer_7_out), .Q(register_3_q), .clk(CLK));  // open: en, clr
  assign REGOUT = STR ? REG00OUT : 8'bz;  // Controlled_Buffer controlled_buffer_9
  and and_7 (and_7_out, controlled_buffer_1_out[1], controlled_buffer_1_out[0]);
  assign REGOUT = STR ? REG01OUT : 8'bz;  // Controlled_Buffer controlled_buffer_10
  assign REGOUT = STR ? REG10OUT : 8'bz;  // Controlled_Buffer controlled_buffer_11
  assign REGOUT = STR ? REG11OUT : 8'bz;  // Controlled_Buffer controlled_buffer_12
  and and_8 (and_8_out, and_7_out, RDM);
  assign controlled_buffer_13_out = and_8_out ? RAMOUT : 8'bz;  // Controlled_Buffer controlled_buffer_13
  Register register_4 (.D(controlled_buffer_13_out), .Q(register_4_q), .clk(CLK));  // open: en, clr
  assign REG11OUT = and_7_out ? register_4_q : 8'bz;  // Controlled_Buffer controlled_buffer_14
endmodule
